// Logisim project Project_1.circ as structural Verilog
module adder_1bit (
  input  A,
  input  B,
  input  Cin,
  output S,
  output Cout
);

  wire and_1_out, and_2_out, xor_1_out;

  xor xor_1 (xor_1_out, A, B);
  xor xor_2 (S, xor_1_out, Cin);
  and and_1 (and_1_out, xor_1_out, Cin);
  and and_2 (and_2_out, A, B);
  or or_1 (Cout, and_1_out, and_2_out);
endmodule

module adder_4bit (
  input  [3:0] A,
  input  Cin,
  input  [3:0] B,
  output [3:0] S,
  output Cout,
  output Overflow
);

  wire adder_1bit_1_cout, adder_1bit_2_cout;

  adder_1bit adder_1bit_1 (.A(A[0]), .B(B[0]), .Cin(Cin), .S(S[0]), .Cout(adder_1bit_1_cout));
  adder_1bit adder_1bit_2 (.A(A[1]), .B(B[1]), .Cin(adder_1bit_1_cout), .S(S[1]), .Cout(adder_1bit_2_cout));
  adder_1bit adder_1bit_3 (.A(A[2]), .B(B[2]), .Cin(adder_1bit_2_cout), .S(S[2]), .Cout(Overflow));
  adder_1bit adder_1bit_4 (.A(A[3]), .B(B[3]), .Cin(Overflow), .S(S[3]), .Cout(Cout));
endmodule

module adder_16bit (
  input  [15:0] A,
  input  in_2,
  input  [15:0] B,
  output [15:0] S,
  output Cout,
  output Overflow
);

  wire adder_4bit_1_cout, adder_4bit_2_cout, adder_4bit_3_cout;

  adder_4bit adder_4bit_1 (.A(A[3:0]), .Cin(in_2), .B(B[3:0]), .S(S[3:0]), .Cout(adder_4bit_1_cout));  // open: Overflow
  adder_4bit adder_4bit_2 (
    .A(A[7:4]), .Cin(adder_4bit_1_cout), .B(B[7:4]), .S(S[7:4]), .Cout(adder_4bit_2_cout));  // open: Overflow
  adder_4bit adder_4bit_3 (
    .A(A[11:8]), .Cin(adder_4bit_2_cout), .B(B[11:8]), .S(S[11:8]), .Cout(adder_4bit_3_cout));  // open: Overflow
  adder_4bit adder_4bit_4 (
    .A(A[15:12]), .Cin(adder_4bit_3_cout), .B(B[15:12]), .S(S[15:12]), .Cout(Cout), .Overflow(Overflow));
endmodule

module add_subtract (
  input  [31:0] A,
  input  Cin,
  input  [31:0] B,
  output [31:0] C,
  output V
);

  wire [31:0] multiplexer_1_out, not_1_out;

  assign not_1_out = ~B;  // NOT_Gate not_1, 32 bits wide
  Multiplexer #(.width(32), .enable("false")) multiplexer_1 (
    .in0(B), .in1(not_1_out), .out(multiplexer_1_out), .sel(Cin));
  Add32 add32_1 (.A(A), .Cin(Cin), .B(multiplexer_1_out), .C(C), .V(V));
endmodule

module gate (
  input  [31:0] A,
  input  [31:0] B,
  input  [3:0] Op,
  output [31:0] C
);

  wire and_1_out, and_2_out, or_1_out;
  wire [31:0] and_3_out, nor_1_out, or_2_out, xor_1_out;

  and and_1 (and_1_out, Op[1], ~Op[2], Op[3]);  // AND_Gate
  and and_2 (and_2_out, ~Op[1], Op[2], ~Op[3]);  // AND_Gate
  or or_1 (or_1_out, and_1_out, and_2_out);
  assign and_3_out = A & B;  // AND_Gate and_3, 32 bits wide
  assign or_2_out = A | B;  // OR_Gate or_2, 32 bits wide
  assign xor_1_out = A ^ B;  // XOR_Gate xor_1, 32 bits wide
  assign nor_1_out = ~(A | B);  // NOR_Gate nor_1, 32 bits wide
  Multiplexer #(.select(2), .width(32)) multiplexer_1 (
    .in0(and_3_out), .in1(or_2_out), .in2(xor_1_out), .in3(nor_1_out), .out(C), .sel(Op[1:0]), .en(or_1_out));

  // Notes on the sheet:
  //   AND
  //   OR
  //   XOR
  //   NOR
endmodule

module compare (
  input  [31:0] B,
  input  [31:0] A,
  input  [3:0] Op,
  output [31:0] C
);

  wire and_1_out, and_2_out, and_3_out, and_4_out, and_5_out, not_2_out, not_3_out, or_1_out;
  wire [31:0] bit_extender_1_out, bit_extender_2_out, bit_extender_3_out, bit_extender_4_out, not_1_out,
       xnor_1_out;

  assign not_1_out = ~A;  // NOT_Gate not_1, 32 bits wide
  assign xnor_1_out = ~(B ^ A);  // XNOR_Gate xnor_1, 32 bits wide
  and and_1 (and_1_out, ~Op[1], ~Op[2], Op[3]);  // AND_Gate
  and and_2 (and_2_out, Op[1], Op[2], Op[3]);
  and and_3 (and_3_out, xnor_1_out[0], xnor_1_out[1], xnor_1_out[2], xnor_1_out[3], xnor_1_out[4], xnor_1_out[5], xnor_1_out[6], xnor_1_out[7], xnor_1_out[8], xnor_1_out[9], xnor_1_out[10], xnor_1_out[11], xnor_1_out[12], xnor_1_out[13], xnor_1_out[14], xnor_1_out[15], xnor_1_out[17], xnor_1_out[18], xnor_1_out[19], xnor_1_out[20], xnor_1_out[21], xnor_1_out[22], xnor_1_out[23], xnor_1_out[24], xnor_1_out[25], xnor_1_out[26], xnor_1_out[27], xnor_1_out[28], xnor_1_out[29], xnor_1_out[30], xnor_1_out[31], xnor_1_out[16]);
  and and_4 (and_4_out, not_1_out[0], not_1_out[1], not_1_out[2], not_1_out[3], not_1_out[4], not_1_out[5], not_1_out[6], not_1_out[7], not_1_out[8], not_1_out[9], not_1_out[10], not_1_out[11], not_1_out[12], not_1_out[13], not_1_out[14], not_1_out[15], not_1_out[17], not_1_out[18], not_1_out[19], not_1_out[20], not_1_out[21], not_1_out[22], not_1_out[23], not_1_out[24], not_1_out[25], not_1_out[26], not_1_out[27], not_1_out[28], not_1_out[29], not_1_out[30], not_1_out[31], not_1_out[16]);
  or or_1 (or_1_out, and_1_out, and_2_out);
  and and_5 (and_5_out, ~A[31], ~and_4_out);  // AND_Gate
  not not_2 (not_2_out, and_3_out);
  not not_3 (not_3_out, and_5_out);
  assign bit_extender_1_out = {{31{1'b0}}, not_2_out};  // Bit_Extender bit_extender_1
  assign bit_extender_2_out = {{31{1'b0}}, and_3_out};  // Bit_Extender bit_extender_2
  assign bit_extender_3_out = {{31{1'b0}}, not_3_out};  // Bit_Extender bit_extender_3
  assign bit_extender_4_out = {{31{1'b0}}, and_5_out};  // Bit_Extender bit_extender_4
  Multiplexer #(.select(2), .width(32)) multiplexer_1 (
    .in0(bit_extender_1_out), .in1(bit_extender_2_out), .in2(bit_extender_3_out), .in3(bit_extender_4_out),
    .out(C), .sel(Op[1:0]), .en(or_1_out));
endmodule

module reflection (
  input  [31:0] B,
  output [31:0] B_reflection,
  output MSB
);


  assign B_reflection = {B[0], B[1], B[2], B[3], B[4], B[5], B[6], B[7], B[8], B[9], B[10], B[11], B[12], B[13], B[14], B[15], B[16], B[17], B[18], B[19], B[20], B[21], B[22], B[23], B[24], B[25], B[26], B[27], B[28], B[29], B[30], B[31]};
  assign MSB = B[31];
endmodule

module shift_1bit (
  input  Cin,
  input  [31:0] B,
  output [31:0] C
);


  assign C = {B[30:0], Cin};
endmodule

module shift_2bit (
  input  in_1,
  input  [31:0] in_2,
  output [31:0] out_3
);

  wire [31:0] shift_1bit_1_c;

  shift_1bit shift_1bit_1 (.Cin(in_1), .B(in_2), .C(shift_1bit_1_c));
  shift_1bit shift_1bit_2 (.Cin(in_1), .B(shift_1bit_1_c), .C(out_3));
endmodule

module shift_4bit (
  input  in_1,
  input  [31:0] in_2,
  output [31:0] out_3
);

  wire [31:0] shift_2bit_1_out_3;

  shift_2bit shift_2bit_1 (.in_1(in_1), .in_2(in_2), .out_3(shift_2bit_1_out_3));
  shift_2bit shift_2bit_2 (.in_1(in_1), .in_2(shift_2bit_1_out_3), .out_3(out_3));
endmodule

module shift_8bit (
  input  in_1,
  input  [31:0] in_2,
  output [31:0] out_3
);

  wire [31:0] shift_4bit_1_out_3;

  shift_4bit shift_4bit_1 (.in_1(in_1), .in_2(in_2), .out_3(shift_4bit_1_out_3));
  shift_4bit shift_4bit_2 (.in_1(in_1), .in_2(shift_4bit_1_out_3), .out_3(out_3));
endmodule

module shift_16bit (
  input  in_1,
  input  [31:0] in_2,
  output [31:0] out_3
);

  wire [31:0] shift_8bit_1_out_3;

  shift_8bit shift_8bit_1 (.in_1(in_1), .in_2(in_2), .out_3(shift_8bit_1_out_3));
  shift_8bit shift_8bit_2 (.in_1(in_1), .in_2(shift_8bit_1_out_3), .out_3(out_3));
endmodule

module LeftShift32 (
  input  [31:0] B,
  input  Cin,
  input  [4:0] Sa,
  output [31:0] C
);

  wire [31:0] multiplexer_1_out, multiplexer_2_out, multiplexer_3_out, multiplexer_4_out, shift_1bit_1_c,
       shift_2bit_1_out_3, shift_4bit_1_out_3, shift_8bit_1_out_3, shift_16bit_1_out_3;

  shift_1bit shift_1bit_1 (.Cin(Cin), .B(B), .C(shift_1bit_1_c));
  Multiplexer #(.width(32), .enable("false")) multiplexer_1 (
    .in0(B), .in1(shift_1bit_1_c), .out(multiplexer_1_out), .sel(Sa[0]));
  shift_2bit shift_2bit_1 (.in_1(Cin), .in_2(multiplexer_1_out), .out_3(shift_2bit_1_out_3));
  Multiplexer #(.width(32), .enable("false")) multiplexer_2 (
    .in0(multiplexer_1_out), .in1(shift_2bit_1_out_3), .out(multiplexer_2_out), .sel(Sa[1]));
  Multiplexer #(.width(32), .enable("false")) multiplexer_3 (
    .in0(multiplexer_2_out), .in1(shift_4bit_1_out_3), .out(multiplexer_3_out), .sel(Sa[2]));
  shift_4bit shift_4bit_1 (.in_1(Cin), .in_2(multiplexer_2_out), .out_3(shift_4bit_1_out_3));
  shift_8bit shift_8bit_1 (.in_1(Cin), .in_2(multiplexer_3_out), .out_3(shift_8bit_1_out_3));
  Multiplexer #(.width(32), .enable("false")) multiplexer_4 (
    .in0(multiplexer_3_out), .in1(shift_8bit_1_out_3), .out(multiplexer_4_out), .sel(Sa[3]));
  Multiplexer #(.width(32), .enable("false")) multiplexer_5 (
    .in0(multiplexer_4_out), .in1(shift_16bit_1_out_3), .out(C), .sel(Sa[4]));
  shift_16bit shift_16bit_1 (.in_1(Cin), .in_2(multiplexer_4_out), .out_3(shift_16bit_1_out_3));
endmodule

module shift (
  input  [31:0] B,
  input  [4:0] Sa,
  input  [3:0] Op,
  output [31:0] C
);

  wire and_1_out, and_2_out, and_3_out, or_1_out, reflection_1_msb;
  wire [31:0] leftshift32_1_c, leftshift32_2_c, reflection_1_b_reflection, reflection_2_b_reflection;

  LeftShift32 leftshift32_1 (.B(B), .Cin(Op[3]), .Sa(Sa), .C(leftshift32_1_c));
  reflection reflection_1 (.B(B), .B_reflection(reflection_1_b_reflection), .MSB(reflection_1_msb));
  and and_1 (and_1_out, reflection_1_msb, Op[0]);
  and and_2 (and_2_out, ~Op[1], ~Op[2], ~Op[3]);  // AND_Gate
  and and_3 (and_3_out, ~Op[1], Op[2], Op[3]);  // AND_Gate
  or or_1 (or_1_out, and_2_out, and_3_out);
  LeftShift32 leftshift32_2 (.B(reflection_1_b_reflection), .Cin(and_1_out), .Sa(Sa), .C(leftshift32_2_c));
  Multiplexer #(.width(32)) multiplexer_1 (
    .in0(leftshift32_1_c), .in1(reflection_2_b_reflection), .out(C), .sel(Op[3]), .en(or_1_out));
  reflection reflection_2 (.B(leftshift32_2_c), .B_reflection(reflection_2_b_reflection));  // open: MSB
endmodule

module ALU32 (
  input  [31:0] A,
  input  [31:0] B,
  input  [3:0] Op,
  input  [4:0] Sa,
  output [31:0] C,
  output V
);

  wire and_1_out;
  wire [31:0] add_subtract_1_c, and_2_out, and_3_out, bit_extender_1_out, compare_1_c, gate_1_c,
       shift_leftright_1_c;

  and and_1 (and_1_out, ~Op[3], Op[1]);  // AND_Gate
  assign bit_extender_1_out = {{31{and_1_out}}, and_1_out};  // Bit_Extender bit_extender_1
  assign and_2_out = A & bit_extender_1_out;  // AND_Gate and_2, 32 bits wide
  assign and_3_out = bit_extender_1_out & B;  // AND_Gate and_3, 32 bits wide
  gate gate_1 (.A(A), .B(B), .Op(Op), .C(gate_1_c));
  compare compare_1 (.B(B), .A(A), .Op(Op), .C(compare_1_c));
  add_subtract add_subtract_1 (.A(and_2_out), .Cin(Op[2]), .B(and_3_out), .C(add_subtract_1_c), .V(V));
  shift_leftright shift_leftright_1 (.B(B), .Op(Op), .Sa(Sa), .C(shift_leftright_1_c));
  assign C = gate_1_c | compare_1_c | add_subtract_1_c | shift_leftright_1_c;  // OR_Gate or_1, 32 bits wide
endmodule

module Add32 (
  input  [31:0] A,
  input  Cin,
  input  [31:0] B,
  output [31:0] C,
  output V
);

  wire adder_16bit_1_cout, adder_16bit_2_cout, adder_16bit_2_overflow;

  adder_16bit adder_16bit_1 (
    .A(A[15:0]), .in_2(Cin), .B(B[15:0]), .S(C[15:0]), .Cout(adder_16bit_1_cout));  // open: Overflow
  adder_16bit adder_16bit_2 (
    .A(A[31:16]), .in_2(adder_16bit_1_cout), .B(B[31:16]), .S(C[31:16]), .Cout(adder_16bit_2_cout),
    .Overflow(adder_16bit_2_overflow));
  xor xor_1 (V, adder_16bit_2_cout, adder_16bit_2_overflow);
endmodule

module shift_leftright (
  input  [31:0] B,
  input  [3:0] Op,
  input  [4:0] Sa,
  output [31:0] C
);

  wire and_1_out, and_2_out, and_3_out, and_4_out, or_1_out, reflection_1_msb;
  wire [4:0] and_5_out, bit_extender_1_out;
  wire [31:0] leftshift32_1_c, multiplexer_1_out, reflection_1_b_reflection, reflection_2_b_reflection;

  reflection reflection_1 (.B(B), .B_reflection(reflection_1_b_reflection), .MSB(reflection_1_msb));
  and and_1 (and_1_out, ~Op[1], ~Op[2], ~Op[3]);  // AND_Gate
  or or_1 (or_1_out, and_1_out, and_2_out);
  and and_2 (and_2_out, ~Op[1], Op[2], Op[3]);  // AND_Gate
  and and_3 (and_3_out, reflection_1_msb, Op[0]);
  Multiplexer #(.width(32)) multiplexer_1 (
    .in0(B), .in1(reflection_1_b_reflection), .out(multiplexer_1_out), .sel(Op[2]), .en(or_1_out));
  assign bit_extender_1_out = {{4{or_1_out}}, or_1_out};  // Bit_Extender bit_extender_1
  and and_4 (and_4_out, and_3_out, Op[2]);
  assign and_5_out = bit_extender_1_out & Sa;  // AND_Gate and_5, 5 bits wide
  LeftShift32 leftshift32_1 (.B(multiplexer_1_out), .Cin(and_4_out), .Sa(and_5_out), .C(leftshift32_1_c));
  Multiplexer #(.width(32), .enable("false")) multiplexer_2 (
    .in0(leftshift32_1_c), .in1(reflection_2_b_reflection), .out(C), .sel(Op[2]));
  reflection reflection_2 (.B(leftshift32_1_c), .B_reflection(reflection_2_b_reflection));  // open: MSB
endmodule
